# Fritzing sketch RFID_parkSystem (saved by Fritzing 0.9.5d)
breadboards: 3

parts:
  A1 = ESP32 DevKitc V4
  HC-SR04_Sensor_1 = HC-SR04 Ultrasonic Distance Sensor
  HC-SR04_Sensor_2 = HC-SR04 Ultrasonic Distance Sensor
  HC-SR04_Sensor_3 = HC-SR04 Ultrasonic Distance Sensor
  Part1 = RFID-RC522-v3
  Part2 = RFID-RC522-v3
  M1 = fc-51 [package=THT]
  M2 = fc-51 [package=THT]
  M3 = Dagu DGServo 9g (Top view) [part_number=RS001B]
  M4 = Dagu DGServo 9g (Top view) [part_number=RS001B]
  A2 = MH-FMD buzzer
  A3 = MH-FMD buzzer
  Part3 = LCD1602-I2C
  R1 = Resistor [tolerance=±5% resistance=220 package=THT]
  R2 = Resistor [tolerance=±5% resistance=220 package=THT]
  R3 = Resistor [tolerance=±5% resistance=220 package=THT]
  R4 = Resistor [tolerance=±5% resistance=220 package=THT]
  R5 = Resistor [tolerance=±5% resistance=220 package=THT]
  R6 = Resistor [tolerance=±5% resistance=220 package=THT]

nets:
  3.3V: A1.Pin_1, Part1.3.3V, Part2.3.3V
  N1: A1.Pin_3, R1.Pin_0, R2.Pin_1
  N2: A1.Pin_4, R3.Pin_0, R4.Pin_0
  N3: A1.Pin_5, M1.pin1
  N4: A1.Pin_6, M2.pin1
  N5: A1.Pin_7, M4.pulse
  N6: A1.Pin_8, Part2.RST
  N7: A1.Pin_9, HC-SR04_Sensor_2.TRIG
  N8: A1.Pin_10, HC-SR04_Sensor_3.TRIG
  N9: A1.Pin_11, HC-SR04_Sensor_1.TRIG
  N10: A1.Pin_12, A2.Pin_2
  GND: A1.Pin_14, A1.Pin_32, A1.Pin_38, HC-SR04_Sensor_1.GND, HC-SR04_Sensor_2.GND, HC-SR04_Sensor_3.GND, Part1.GND, Part2.GND, M1.pin2, M2.pin2, M3.gnd, M4.gnd, A2.Pin_3, A3.Pin_3, Part3.GND, R2.Pin_0, R4.Pin_1, R6.Pin_1
  N11: A1.Pin_15, R5.Pin_0, R6.Pin_0
  VCC: A1.Pin_19, HC-SR04_Sensor_1.VCC, HC-SR04_Sensor_2.VCC, HC-SR04_Sensor_3.VCC, M1.pin3, M2.pin3, M3.vcc, M4.vcc, A2.Pin_1, A3.Pin_1, Part3.VCC
  N12: A1.Pin_23, A3.Pin_2
  N13: A1.Pin_26, M3.pulse
  N14: A1.Pin_27, Part1.RST
  N15: A1.Pin_28, Part2.SDA
  N16: A1.Pin_29, Part1.SDA
  N17: A1.Pin_30, Part1.SCK, Part2.SCK
  N18: A1.Pin_31, Part1.MISO, Part2.MISO
  N19: A1.Pin_33, Part3.SDA
  N20: A1.Pin_36, Part3.SCL
  N21: A1.Pin_37, Part1.MOSI, Part2.MOSI
  N22: HC-SR04_Sensor_1.ECHO, R1.Pin_1
  N23: HC-SR04_Sensor_2.ECHO, R5.Pin_1
  N24: HC-SR04_Sensor_3.ECHO, R3.Pin_1

custom parts:
  ESP32 DevKitc V4: ESP32-DevKitC board with ESP32-WROOM-32 module. ESP32-DevKitC V4 is a small-sized ESP32-based development board produced by Espressif. Most of the pins on the ESP module are broken out to the pin headers on the board. The pins D0, D1, D2, D3, CMD and CLK are used internally for communication between ESP32 and SPI flash memory. They are grouped on both sides near the USB connector. Avoid using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
  RFID-RC522-v3: A simple China made RFID-RC522 Reader (6x4 cm); do check the pin labels, as this is a MFRC522 based clone.
  MH-FMD buzzer: MH-FMD buzzer.
  LCD1602-I2C: A standard character display, usually with 2x16 characters. Comes in many colors with LCM1602 IIC attached.
